// Logisim project MMFINALupdated.circ as structural Verilog: 3 circuits, main circuit main
module main (
  input  in_1,
  output out_2
);

  wire clock_1_out, INC_PC, LoadAC, LoadAR, LoadDR, loadIR, LoadPC, nor_1_out, Read_MEM, Write_MEM;
  wire [2:0] ALUcon, bus, IR_q_2;
  wire [6:0] AR_q, bit_extender_1_out, bit_extender_2_out, PC_q;
  wire [15:0] AC_q, alu_1_ac_output, bit_extender_3_out, bit_extender_4_out, DR_q, IR_q, multiplexer_1_out,
       ram_1_data, TR_q;

  Bit_Extender #(.in_width(16), .out_width(7)) bit_extender_1 (.in(multiplexer_1_out), .out(bit_extender_1_out));
  Clock clock_1 (.out(clock_1_out));
  Bit_Extender #(.in_width(16), .out_width(7)) bit_extender_2 (.in(multiplexer_1_out), .out(bit_extender_2_out));
  Register #(.width(7)) AR (.D(bit_extender_1_out), .en(LoadAR), .Q(AR_q), .clk(clock_1_out));  // open: clr
  Register #(.width(16)) TR (.D(multiplexer_1_out), .Q(TR_q), .clk(clock_1_out));  // open: en, clr
  Register #(.width(16)) DR (.D(multiplexer_1_out), .en(LoadDR), .Q(DR_q), .clk(clock_1_out));  // open: clr
  Register #(.width(16)) AC (.D(alu_1_ac_output), .en(LoadAC), .Q(AC_q), .clk(clock_1_out));  // open: clr
  Counter #(.width(7), .max('h7f)) PC (
    .load(LoadPC), .D(bit_extender_2_out), .count(INC_PC), .Q(PC_q), .clk(clock_1_out));  // open: carry, clr
  RAM #(.addrWidth(7), .dataWidth(16), .bus("separate")) ram_1 (
    .addr(AR_q), .din(multiplexer_1_out), .data(ram_1_data), .str(Write_MEM), .clk(clock_1_out), .ld(Read_MEM));  // open: sel, clr
  assign bit_extender_3_out = {{9{1'b0}}, PC_q};  // Bit_Extender bit_extender_3
  assign bit_extender_4_out = {{9{1'b0}}, AR_q};  // Bit_Extender bit_extender_4
  ALU alu_1 (.A(DR_q), .B(AC_q), .in_3(ALUcon), .E(out_2), .AC_Output(alu_1_ac_output));
  Register #(.width(16)) IR (
    .D(multiplexer_1_out), .en(loadIR), .Q({IR_q[15], IR_q_2, IR_q[11:0]}), .clk(clock_1_out));  // open: clr
  nor nor_1 (nor_1_out, AC_q[0], AC_q[1], AC_q[2], AC_q[3], AC_q[4], AC_q[5], AC_q[6], AC_q[7], AC_q[9], AC_q[10], AC_q[11], AC_q[12], AC_q[13], AC_q[14], AC_q[15], AC_q[8]);
  Multiplexer #(.select(3), .width(16)) multiplexer_1 (
    .in0(ram_1_data), .in1(bit_extender_4_out), .in2(TR_q), .in3(DR_q), .in4(AC_q), .in5(bit_extender_3_out),
    .in6({IR_q[15], IR_q_2, IR_q[11:0]}), .out(multiplexer_1_out), .sel(bus));  // open: in7, en
  ControlUnit controlunit_1 (
    .Bits_12_14(IR_q_2), .Bit_15(IR_q[15]), .AC_0(nor_1_out), .CLK(clock_1_out), .Bits_0_11(IR_q[11:0]),
    .in_6(in_1), .in_7(in_1), .LoadAC(LoadAC), .LoadAR(LoadAR), .INC_PC(INC_PC), .LoadPC(LoadPC),
    .LoadIR(loadIR), .Write_MEM(Write_MEM), .LoadDR(LoadDR), .Read_MEM(Read_MEM), .selectionbus(bus),
    .selectionALU(ALUcon));
endmodule

module ALU (
  input  [15:0] A,
  input  [15:0] B,
  input  [2:0] in_3,
  output E,
  output [15:0] AC_Output
);

  wire adder_1_cout, adder_2_cout, subtractor_1_bout;
  wire [15:0] adder_1_out, adder_2_out, and_1_out, or_1_out, subtractor_1_out, xor_1_out;

  Adder #(.width(16)) adder_1 (.a(A), .b(B), .out(adder_1_out), .cin(1'b0), .cout(adder_1_cout));
  Subtractor #(.width(16)) subtractor_1 (.a(A), .b(B), .out(subtractor_1_out), .bin(1'b0), .bout(subtractor_1_bout));
  assign and_1_out = A & B;  // AND_Gate and_1, 16 bits wide
  assign or_1_out = A | B;  // OR_Gate or_1, 16 bits wide
  assign xor_1_out = A ^ B;  // XOR_Gate xor_1, 16 bits wide
  Adder #(.width(16)) adder_2 (.a(A), .b({16{1'b0}}), .out(adder_2_out), .cin(1'b1), .cout(adder_2_cout));
  or or_2 (E, adder_1_cout, subtractor_1_bout, adder_2_cout);
  Multiplexer #(.select(3), .width(16)) multiplexer_1 (
    .in1(adder_1_out), .in2(subtractor_1_out), .in3(A), .in4(and_1_out), .in5(or_1_out), .in6(xor_1_out),
    .in7(adder_2_out), .out(AC_Output), .sel(in_3));  // open: in0, en
endmodule

module ControlUnit (
  input  [2:0] Bits_12_14,
  input  Bit_15,
  input  AC_0,
  input  CLK,
  input  [11:0] Bits_0_11,
  input  in_6,
  input  in_7,
  output LoadAC,
  output LoadAR,
  output INC_PC,
  output LoadPC,
  output LoadIR,
  output Write_MEM,
  output LoadDR,
  output Read_MEM,
  output [2:0] selectionbus,
  output [2:0] selectionALU
);

  wire addALU, and_6_out, and_7_out, and_8_out, and_9_out, and_10_out, and_11_out, and_12_out, and_14_out,
       and_20_out, and_25_out, and_26_out, and_29_out, and_30_out, andALU, busAC, busAR, busIR, busMEM,
       busPC, CLR_SC, D0, D0T4, D0T5, D1, D2, D3, D3T4, D4, D5, D6, D7, D7I_prime_T3B5, D7I_prime_T4B5,
       d_ff_1_q, I_prime, incALU, r, subALU, T3, T4, T4D1, T4D2, T4D4, T4D5, T5, T5D1, T5D2, T5D5, T6, T7,
       T8, T9, T10, T11, T12, T13, T14, T15, transferALU;
  wire [3:0] counter_1_q;

  Counter #(.width(4), .max('hf)) counter_1 (
    .Q(counter_1_q), .clk(CLK), .clr(d_ff_1_q));  // open: load, D, count, carry
  and and_1 (D0T4, D0, T4);
  and and_2 (T4D2, T4, D2);
  and and_3 (T4D1, T4, D1);
  and and_4 (T4D5, T4, D5);
  not not_1 (I_prime, Bit_15);
  D_Flip_Flop d_ff_1 (.clk(CLK), .D(CLR_SC), .Q(d_ff_1_q));  // open: Qn, preset, en, reset
  and and_5 (r, D7, I_prime, T3);
  and and_6 (and_6_out, r, Bits_0_11[5]);
  Decoder #(.select(3)) decoder_1 (
    .out0(D0), .out1(D1), .out2(D2), .out3(D3), .out4(D4), .out5(D5), .out6(D6), .out7(D7), .sel(Bits_12_14));  // open: en
  Decoder #(.select(4)) decoder_2 (
    .out0(busPC), .out1(LoadIR), .out2(busIR), .out3(T3), .out4(T4), .out5(T5), .out6(T6), .out7(T7),
    .out8(T8), .out9(T9), .out10(T10), .out11(T11), .out12(T12), .out13(T13), .out14(T14), .out15(T15),
    .sel(counter_1_q));  // open: en
  or u_LoadDR (LoadDR, D7I_prime_T3B5, T4D2, T4D1, and_6_out, D0T4, T4D5, T5D5);
  and and_7 (and_7_out, T4, D2);
  and and_8 (and_8_out, T4, D1);
  and and_9 (and_9_out, D0, T4);
  and and_10 (and_10_out, T4, D5);
  and and_11 (and_11_out, r, Bits_0_11[5]);
  or or_1 (busMEM, LoadIR, and_7_out, and_9_out, and_8_out, and_10_out);
  and and_12 (and_12_out, T5, D2);
  or or_2 (transferALU, and_12_out, T5D5);
  and and_13 (addALU, T5, D1);
  and and_14 (and_14_out, D3, T4);
  and and_15 (busAR, T4, D4);
  and and_16 (andALU, T5, D0);
  or or_3 (busAC, T5D5, and_11_out, and_14_out);
  and and_17 (subALU, T6, D5);
  and and_18 (incALU, D7, I_prime, T4);
  and and_19 (T5D5, T5, D5);
  and and_20 (and_20_out, r, Bits_0_11[2]);
  and and_21 (D0T5, D0, T5);
  and and_22 (T5D1, T5, D1);
  and and_23 (T5D2, T5, D2);
  and and_24 (T4D4, T4, D4);
  and and_25 (and_25_out, T6, D5);
  and u_LoadPC (LoadPC, D4, T4);
  and u_Write_MEM (Write_MEM, D3, T4);
  and and_26 (and_26_out, T6, D5);
  or u_Read_MEM (Read_MEM, LoadIR, T4D2, T4D1, T4D5, D0T4);
  Priority_Encoder priority_encoder_1 (
    .in0(busMEM), .in1(busAR), .in2(in_6), .in3(in_6), .in4(busAC), .in5(busPC), .in6(busIR), .in7(in_6),
    .out(selectionbus));  // open: en_in, gs, en_out
  and and_27 (D7I_prime_T3B5, D7, I_prime, T3, Bits_0_11[5]);
  or u_LoadAC (LoadAC, D7I_prime_T4B5, T5D1, T5D2, D0T5, T5D5, and_25_out);
  and and_28 (D7I_prime_T4B5, D7, I_prime, T4, Bits_0_11[5]);
  and Write_MEM_2 (D3T4, D3, T4);
  or or_4 (CLR_SC, T4D4, T5D2, T5D1, and_29_out, D0T5, D3T4, and_20_out, and_26_out);
  and and_29 (and_29_out, D7, I_prime, T4);
  Priority_Encoder priority_encoder_2 (
    .in0(in_7), .in1(addALU), .in2(subALU), .in3(transferALU), .in4(andALU), .in5(in_7), .in6(in_7),
    .in7(incALU), .out(selectionALU));  // open: en_in, gs, en_out
  and and_30 (and_30_out, r, AC_0, Bits_0_11[2]);
  or or_5 (LoadAR, busIR, T4D2, T4D1, T4D5, D0T4, busPC);
  or or_6 (INC_PC, LoadIR, and_30_out);

  // Other names for the same wires on the sheet: AC0 = AC_0; B2 = Bits_0_11[2]; B5 = Bits_0_11[5]; T2 = busIR;
  //   T0 = busPC; T1 = LoadIR
endmodule
